# Fritzing sketch zegar_startowy (saved by Fritzing 0.9.0b)
circuit board: 8.46667cm x 5.64444cm
breadboards: 1

parts:
  Part1 = Arduino Uno (Rev3)
  12V = Power plug
  display_driver = Generic shrouded header - 10 pins [form="♂ (shrouded male)" package=THT]
  switch_display = SPST Switch [package=r_sw_th]
  TX/RX = female pin header, 2 pins [form="♀ (female)"]
  switch_power = SPST Switch [package=r_sw_th]
  J1 = Piezo Speaker
  Q6 = NPN-Transistor [package="TO92 [THT]"]
  switch_buzzer = SPST Switch [package=r_sw_th]
  S_UP = Square Pushbutton
  S_SET = Square Pushbutton
  S_MODE = Square Pushbutton
  S_DOWN = Square Pushbutton

nets (from the schematic view):
  N1: Part1.A0, S_UP.leg1
  N2: Part1.A1, S_DOWN.leg1
  N3: Part1.A2, S_SET.leg1
  N4: Part1.A3, S_MODE.leg1
  N5: Part1.D10_PWM/SS, display_driver.RCK
  N6: Part1.D11_PWM/MOSI, display_driver.SER_IN
  N7: Part1.D13/SCK, display_driver.SRCK
  GND: Part1.GND, 12V.GND, display_driver.GND, Q6.E
  N8: Part1.D0/RX, TX/RX.pin1
  N9: Part1.D1/TX, TX/RX.pin2
  N10: Part1.D2, Q6.B
  5V: Part1.5V, display_driver.VCC
  N11: Part1.VIN, switch_display.P, switch_power.O, switch_buzzer.P
  N12: 12V.VCC, switch_power.P
  N13: display_driver.12V, switch_display.O
  N14: J1.pin1, Q6.C
  N15: J1.pin2, switch_buzzer.O
  N16: S_UP.leg0, S_SET.leg0, S_MODE.leg0, S_DOWN.leg0

custom parts:
  Generic shrouded header - 10 pins: Generic shrouded header
